# Fritzing sketch Arduino_Tutorial (saved by Fritzing 0.8.7b)
breadboards: 1

parts:
  Part1 = Arduino Uno (Rev3) - ICSP
  LED1 = RGB LED (com. anode, rbg) [package="5 mm [THT]"]
  R1 = Resistor [tolerance=±5% resistance=220 package=THT]
  R2 = Resistor [tolerance=±5% resistance=220 package=THT]
  R3 = Resistor [tolerance=±5% resistance=220 package=THT]

nets:
  N1: Part1.GND, R1.Pin_0, R2.Pin_1, R3.Pin_1
  N2: Part1.5V, LED1.common_anode
  N3: LED1.red_cathode, R1.Pin_1
  N4: LED1.blue_cathode, R3.Pin_0
  N5: LED1.green_cathode, R2.Pin_0
